# Fritzing sketch so-do-dau-mach (saved by Fritzing 1.0.6)

parts:
  M1 = RioRand LM2596
  Power_plug1 = Power plug
  Fuse1 = Fuse with Handler [part_number=Htc-15m]
  M2 = RioRand LM2596
  Power_plug2 = Power plug
  Fuse2 = Fuse with Handler [part_number=Htc-15m]

nets:
  N1: M1.Pin_1, Fuse1.Connector2
  N2: Power_plug1.VCC, Fuse1.Connector1
  N3: M2.Pin_1, Fuse2.Connector2
  N4: Power_plug2.VCC, Fuse2.Connector1

notes:
  5v
  12V - 24V
  Mạch hạ áp
  GND
  chung GND
  DATA
  [write your notehgjgh herghje]
  ghjgfwrite your note here]
